# Fritzing sketch iot-arduino-counter1 (saved by Fritzing 0.9.9b)
breadboards: 1

parts:
  Bauteil1 = Arduino Uno (Rev3)
  ICM1 = 7555 [part_number=7555 package="DIP (Dual Inline) [THT]"]
  R3 = Resistor [tolerance=±5% power=0.25 resistance=180k package=THT]
  S1 = Pushbutton [package="[THT]"]
  R4 = Resistor [tolerance=±5% power=0.25 resistance=2.2k package=THT]
  C1 = Ceramic Capacitor [capacitance=100nF voltage=35V package="100 mil [THT, multilayer]"]
  LED1 = LED - 5mm [color="Red (633nm)" current=0.030 package="5 mm [THT]"]
  R5 = Resistor [tolerance=±5% power=0.25 resistance=560 package=THT]

nets (from the breadboard view):
  N1: Bauteil1.D5_PWM, ICM1.Output, LED1.anode
  5V: Bauteil1.5V, ICM1.Reset, ICM1.Control, ICM1.VDD, R4.Pin_1
  GND: Bauteil1.GND, ICM1.GND, S1.Pin_1, S1.Pin_2, C1.0, R5.Pin_1
  N2: ICM1.Trigger, ICM1.Threshold, R3.Pin_0, C1.1
  N3: R3.Pin_1, S1.Pin_3, S1.Pin_4, R4.Pin_0
  N4: LED1.cathode, R5.Pin_0

notes:
  iot-arduino-counter1
  180kΩ
  2.2kΩ
  100nF
  Schmitt-Trigger

custom parts:
  7555: General purpose CMOS timer
