# Fritzing sketch iot-arduino-interrupt1 (saved by Fritzing 0.9.9b)
circuit board: 7.75924cm x 5.31154cm
breadboards: 1

parts:
  Bauteil1 = Arduino Uno (Rev3)
  S1 = Pushbutton [package="[THT]"]
  LED2_(rot) = LED - 5mm [color="Red (633nm)" current=30mA package="5 mm [THT]"]
  R2 = Resistor [tolerance=±5% power=0.25 resistance=220 package=THT]

nets (from the breadboard view):
  N1: Bauteil1.D13/SCK, LED2_(rot).anode
  N2: Bauteil1.D2, S1.Pin_3, S1.Pin_4
  N3: Bauteil1.GND, S1.Pin_1, S1.Pin_2, R2.Pin_0
  N4: LED2_(rot).cathode, R2.Pin_1

notes:
  iot-arduino-interrupt1
