# Fritzing sketch arduino_avr_rtosMega (saved by Fritzing 0.9.10b)
breadboards: 2

parts:
  LED1 = LED - 5mm [color="Red (633nm)" current=0.030 package="5 mm [THT]"]
  LED2 = LED - 5mm [color="Yellow (595nm)" current=0.030 package="5 mm [THT]"]
  R4 = Resistor [tolerance=±5% power=0.25 resistance=560 package=THT]
  R5 = Resistor [tolerance=±5% power=0.25 resistance=560 package=THT]
  LED3 = LED - 5mm [color="Green (555nm)" current=0.030 package="5 mm [THT]"]
  R6 = Resistor [tolerance=±5% power=0.25 resistance=560 package=THT]
  R7 = Trimmer Potentiometer [maximum_resistance=10kΩ knob_status=50% power=0.5W package=THT]
  R8 = Trimmer Potentiometer [maximum_resistance=10kΩ knob_status=50% power=0.5W package=THT]
  S1 = Pushbutton [package="[THT]"]
  S2 = Pushbutton [package="[THT]"]
  S3 = Pushbutton [package="[THT]"]
  C5 = Ceramic Capacitor [capacitance=100nF voltage=35V package="100 mil [THT, multilayer]"]
  Bauteil2 = Arduino Mega 2560 (Rev3)
  LCD1 = LCD screen
  R9 = Resistor [tolerance=±5% power=0.25 resistance=220 package=THT]
  R10 = Trimmer Potentiometer [maximum_resistance=10kΩ knob_status=50% power=0.5W package=THT]

nets:
  N1: LED1.cathode, R6.Pin_0
  N2: LED1.anode, Bauteil2.D12_PWM
  N3: LED2.cathode, R5.Pin_0
  N4: LED2.anode, Bauteil2.D11_PWM
  N5: R4.Pin_0, LED3.cathode
  GND: R4.Pin_1, R5.Pin_1, R6.Pin_1, R7.leg1, R8.leg1, S1.Pin_1, S1.Pin_2, S2.Pin_1, S2.Pin_2, S3.Pin_1, S3.Pin_2, C5.0, Bauteil2.GND, LCD1.VSS, LCD1.R/W, LCD1.LED-, R10.leg2
  N6: LED3.anode, Bauteil2.D10_PWM
  N7: R7.wiper, Bauteil2.A0
  N8: R7.leg2, R8.leg2, C5.1, Bauteil2.A2, Bauteil2.3V3
  N9: R8.wiper, Bauteil2.A1
  N10: S1.Pin_3, S1.Pin_4, Bauteil2.D4_PWM
  N11: S2.Pin_3, S2.Pin_4, Bauteil2.D3_PWM
  N12: S3.Pin_3, S3.Pin_4, Bauteil2.D2_PWM
  5V: Bauteil2.5V, LCD1.VDD, R9.Pin_0, R10.leg1
  N13: Bauteil2.D40, LCD1.DB7
  N14: Bauteil2.D42, LCD1.DB6
  N15: Bauteil2.D44, LCD1.DB5
  N16: Bauteil2.D46, LCD1.DB4
  N17: Bauteil2.D48, LCD1.E
  N18: Bauteil2.D50, LCD1.RS
  N19: LCD1.V0, R10.wiper
  N20: LCD1.LED+, R9.Pin_1

notes:
  arduino_avr_rtosMega
  red
  gelb
  grün
