# Fritzing sketch arduino_avr_rtosTask01 (saved by Fritzing 0.9.10b)
breadboards: 1

parts:
  Bauteil1 = Arduino Uno (Rev3)
  LED1 = LED - 5mm [color="Red (633nm)" current=0.030 package="5 mm [THT]"]
  LED2 = LED - 5mm [color="Yellow (595nm)" current=0.030 package="5 mm [THT]"]
  R5 = Resistor [tolerance=±5% power=0.25 resistance=560 package=THT]
  R6 = Resistor [tolerance=±5% power=0.25 resistance=560 package=THT]
  R7 = Trimmer Potentiometer [maximum_resistance=10kΩ knob_status=50% power=0.5W package=THT]
  R8 = Trimmer Potentiometer [maximum_resistance=10kΩ knob_status=50% power=0.5W package=THT]
  C1 = Ceramic Capacitor [capacitance=100nF voltage=35V package="100 mil [THT, multilayer]"]
  C2 = Ceramic Capacitor [capacitance=100nF voltage=35V package="100 mil [THT, multilayer]"]
  C5 = Ceramic Capacitor [capacitance=100nF voltage=35V package="100 mil [THT, multilayer]"]

nets:
  N1: Bauteil1.A0, R7.wiper, C1.1
  N2: Bauteil1.A1, R8.wiper, C2.1
  N3: Bauteil1.D3_PWM, LED2.anode
  N4: Bauteil1.D4, LED1.anode
  N5: Bauteil1.5V, R7.leg2, R8.leg2, C5.1
  N6: Bauteil1.GND, R5.Pin_1, R6.Pin_1, R7.leg1, R8.leg1, C1.0, C2.0, C5.0
  N7: LED1.cathode, R6.Pin_0
  N8: LED2.cathode, R5.Pin_0

notes:
  arduino_avr_rtosTask01
  rot
  gelb
  z.B. 100nF
