# Fritzing sketch iot-arduino-softwareTimer1 (saved by Fritzing 0.9.9b)
circuit board: 7.75924cm x 5.31154cm
breadboards: 1

parts:
  Bauteil1 = Arduino Uno (Rev3)
  LED2_(rot) = LED - 5mm [color="Red (633nm)" current=30mA package="5 mm [THT]"]
  LED1_(grün) = smd LED [color="Green (555nm)" current=0.030 package="0805 [SMD]"]
  R1 = Resistor [tolerance=±5% power=0.25 resistance=220 package=THT]
  R2 = Resistor [tolerance=±5% power=0.25 resistance=220 package=THT]

nets (from the schematic view):
  N1: Bauteil1.D10_PWM/SS, LED1_(grün).anode
  N2: Bauteil1.D12/MISO, LED2_(rot).anode
  N3: Bauteil1.GND, R1.Pin_0, R2.Pin_0
  N4: LED2_(rot).cathode, R2.Pin_1
  N5: LED1_(grün).cathode, R1.Pin_1

notes:
  iot-arduino-timer1
